# Fritzing sketch hello_lcd (saved by Fritzing 0.9.9b)
breadboards: 1

parts:
  R1 = Trimmer Potentiometer [maximum_resistance=10kΩ package=THT]
  U1 = LCD-16X2 [package=lcd-16x2_noholes]
  パーツ1 = Arduino Uno (Rev3)

nets:
  VDD: R1.leg1, U1.VDD, U1.A, パーツ1.5V
  N1: R1.wiper, U1.VO
  VSS: R1.leg2, U1.VSS, U1.R_W, U1.K, パーツ1.GND
  N2: U1.RS, パーツ1.D7
  N3: U1.E, パーツ1.D8
  N4: U1.DB4, パーツ1.D9_PWM
  N5: U1.DB5, パーツ1.D10_PWM/SS
  N6: U1.DB6, パーツ1.D11_PWM/MOSI
  N7: U1.DB7, パーツ1.D12/MISO

notes:
  LCDの向きが反転してるので注意
  可変抵抗はLCDのコントラスト調整用。
  適当な抵抗を差し替えて調整でもいける。
