# Fritzing sketch sensor_and_lcd (saved by Fritzing 0.9.9b)
breadboards: 1

parts:
  R1 = Trimmer Potentiometer [maximum_resistance=10kΩ package=THT]
  U1 = LCD-16X2 [package=lcd-16x2_noholes]
  パーツ1 = Arduino Uno (Rev3)
  HC-SR04_Sensor_1 = HC-SR04 Ultrasonic Distance Sensor

nets:
  VDD: R1.leg1, U1.VDD, U1.A, パーツ1.5V, HC-SR04_Sensor_1.VCC
  N1: R1.wiper, U1.VO
  GND: R1.leg2, U1.VSS, U1.R_W, U1.K, パーツ1.GND, HC-SR04_Sensor_1.GND
  N2: U1.RS, パーツ1.D7
  N3: U1.E, パーツ1.D8
  N4: U1.DB4, パーツ1.D9_PWM
  N5: U1.DB5, パーツ1.D10_PWM/SS
  N6: U1.DB6, パーツ1.D11_PWM/MOSI
  N7: U1.DB7, パーツ1.D12/MISO
  N8: パーツ1.D2, HC-SR04_Sensor_1.ECHO
  N9: パーツ1.D3_PWM, HC-SR04_Sensor_1.TRIG

notes:
  LCDの向きが反転してるので注意
