# Fritzing sketch sonic_sensor (saved by Fritzing 0.9.9b)
breadboards: 1

parts:
  パーツ1 = Arduino Uno (Rev3)
  HC-SR04_Sensor_1 = HC-SR04 Ultrasonic Distance Sensor

nets:
  GND: パーツ1.GND, HC-SR04_Sensor_1.GND
  N1: パーツ1.D2, HC-SR04_Sensor_1.ECHO
  N2: パーツ1.D3_PWM, HC-SR04_Sensor_1.TRIG
  5V: パーツ1.5V, HC-SR04_Sensor_1.VCC
